// Logisim project COMP273Assignment1Q4.circ as structural Verilog: 11 circuits, main circuit main
module main (
  input  A0,
  input  A1,
  input  A2,
  input  A3,
  input  B0,
  input  B1,
  input  B2,
  input  B3,
  input  C0,
  input  C1,
  input  C2,
  input  C3,
  output R0,
  output R1,
  output R2,
  output R3,
  output OVERFLOW,
  output ZERO
);

  wire add_1_overflow, add_1_r0, add_1_r1, add_1_r2, add_1_r3, and_1_r0, and_1_r1, and_1_r2, and_1_r3,
       n4_bit_control_signal_decoder_1_add, n4_bit_control_signal_decoder_1_and,
       n4_bit_control_signal_decoder_1_nor, n4_bit_control_signal_decoder_1_or,
       n4_bit_control_signal_decoder_1_slt, n4_bit_control_signal_decoder_1_sub, nor_1_r0, nor_1_r1,
       nor_1_r2, nor_1_r3, not_1_out, not_2_out, not_3_out, not_4_out, or_1_r0, or_1_r1, or_1_r2, or_1_r3,
       slt_1_overflow, slt_1_r0, slt_1_r1, slt_1_r2, slt_1_r3, SUB_overflow, SUB_r0, SUB_r1, SUB_r2, SUB_r3;
  wire [4:0] n5_signal_selector_1_r0, n5_signal_selector_2_r0, n5_signal_selector_3_r0,
       n5_signal_selector_4_r0, n5_signal_selector_5_r0, n5_signal_selector_6_r0;

  // Probe on {A3, A2, A1, A0}
  // Probe on {B3, B2, B1, B0}
  _4_bit_control_signal_decoder u_4_bit_control_signal_decoder_1 (
    .C0(C0), .C1(C1), .C2(C2), .C3(C3), .AND(n4_bit_control_signal_decoder_1_and),
    .OR(n4_bit_control_signal_decoder_1_or), .ADD(n4_bit_control_signal_decoder_1_add),
    .SUB(n4_bit_control_signal_decoder_1_sub), .SLT(n4_bit_control_signal_decoder_1_slt),
    .NOR(n4_bit_control_signal_decoder_1_nor));  // open: out_5
  // Probe on {C3, C2, C1, C0}
  not not_1 (not_1_out, n4_bit_control_signal_decoder_1_and);
  AND and_1 (
    .A0(A0), .A1(A1), .A2(A2), .A3(A3), .B0(B0), .B1(B1), .B2(B2), .B3(B3), .R0(and_1_r0), .R1(and_1_r1),
    .R2(and_1_r2), .R3(and_1_r3));
  _5_signal_selector u_5_signal_selector_1 (
    ._0(and_1_r0), ._1(and_1_r1), ._2(and_1_r2), ._3(and_1_r3), .OVERFLOW(not_1_out),
    .S(n4_bit_control_signal_decoder_1_and), .R0(n5_signal_selector_1_r0[0]),
    .R1(n5_signal_selector_1_r0[1]), .R2(n5_signal_selector_1_r0[2]), .R3(n5_signal_selector_1_r0[3]),
    .OVERFLOW_2(n5_signal_selector_1_r0[4]));
  not not_2 (not_2_out, n4_bit_control_signal_decoder_1_or);
  OR or_1 (
    .A0(A0), .A1(A1), .A2(A2), .A3(A3), .B0(B0), .B1(B1), .B2(B2), .B3(B3), .R0(or_1_r0), .R1(or_1_r1),
    .R2(or_1_r2), .R3(or_1_r3));
  _5_signal_selector u_5_signal_selector_2 (
    ._0(or_1_r0), ._1(or_1_r1), ._2(or_1_r2), ._3(or_1_r3), .OVERFLOW(not_2_out),
    .S(n4_bit_control_signal_decoder_1_or), .R0(n5_signal_selector_2_r0[0]), .R1(n5_signal_selector_2_r0[1]),
    .R2(n5_signal_selector_2_r0[2]), .R3(n5_signal_selector_2_r0[3]), .OVERFLOW_2(n5_signal_selector_2_r0[4]));
  ADD add_1 (
    .CONTROL(not_3_out), .A0(A0), .A1(A1), .A2(A2), .A3(A3), .B0(B0), .B1(B1), .B2(B2), .B3(B3),
    .R0(add_1_r0), .R1(add_1_r1), .R2(add_1_r2), .R3(add_1_r3), .OVERFLOW(add_1_overflow));
  _5_signal_selector u_5_signal_selector_3 (
    ._0(add_1_r0), ._1(add_1_r1), ._2(add_1_r2), ._3(add_1_r3), .OVERFLOW(add_1_overflow),
    .S(n4_bit_control_signal_decoder_1_add), .R0(n5_signal_selector_3_r0[0]),
    .R1(n5_signal_selector_3_r0[1]), .R2(n5_signal_selector_3_r0[2]), .R3(n5_signal_selector_3_r0[3]),
    .OVERFLOW_2(n5_signal_selector_3_r0[4]));
  not not_3 (not_3_out, n4_bit_control_signal_decoder_1_add);
  SUB SUB (
    .A0(A0), .A1(A1), .A2(A2), .A3(A3), .B0(B0), .B1(B1), .B2(B2), .B3(B3), .R0(SUB_r0), .R1(SUB_r1),
    .R2(SUB_r2), .R3(SUB_r3), .OVERFLOW(SUB_overflow));
  _5_signal_selector u_5_signal_selector_4 (
    ._0(SUB_r0), ._1(SUB_r1), ._2(SUB_r2), ._3(SUB_r3), .OVERFLOW(SUB_overflow),
    .S(n4_bit_control_signal_decoder_1_sub), .R0(n5_signal_selector_4_r0[0]),
    .R1(n5_signal_selector_4_r0[1]), .R2(n5_signal_selector_4_r0[2]), .R3(n5_signal_selector_4_r0[3]),
    .OVERFLOW_2(n5_signal_selector_4_r0[4]));
  SLT slt_1 (
    .A0(A0), .A1(A1), .A2(A2), .A3(A3), .B0(B0), .B1(B1), .B2(B2), .B3(B3), .R0(slt_1_r0), .R1(slt_1_r1),
    .R2(slt_1_r2), .R3(slt_1_r3), .OVERFLOW(slt_1_overflow));
  _5_signal_selector u_5_signal_selector_5 (
    ._0(slt_1_r0), ._1(slt_1_r1), ._2(slt_1_r2), ._3(slt_1_r3), .OVERFLOW(slt_1_overflow),
    .S(n4_bit_control_signal_decoder_1_slt), .R0(n5_signal_selector_5_r0[0]),
    .R1(n5_signal_selector_5_r0[1]), .R2(n5_signal_selector_5_r0[2]), .R3(n5_signal_selector_5_r0[3]),
    .OVERFLOW_2(n5_signal_selector_5_r0[4]));
  NOR nor_1 (
    .A0(A0), .A1(A1), .A2(A2), .A3(A3), .B0(B0), .B1(B1), .B2(B2), .B3(B3), .R0(nor_1_r0), .R1(nor_1_r1),
    .R2(nor_1_r2), .R3(nor_1_r3));
  not not_4 (not_4_out, n4_bit_control_signal_decoder_1_nor);
  _5_signal_selector u_5_signal_selector_6 (
    ._0(nor_1_r0), ._1(nor_1_r1), ._2(nor_1_r2), ._3(nor_1_r3), .OVERFLOW(not_4_out),
    .S(n4_bit_control_signal_decoder_1_nor), .R0(n5_signal_selector_6_r0[0]),
    .R1(n5_signal_selector_6_r0[1]), .R2(n5_signal_selector_6_r0[2]), .R3(n5_signal_selector_6_r0[3]),
    .OVERFLOW_2(n5_signal_selector_6_r0[4]));
  _5_signl_merger u_5_signl_merger_1 (
    .in_1(n5_signal_selector_6_r0), .in_2(n5_signal_selector_5_r0), .in_3(n5_signal_selector_4_r0),
    .in_4(n5_signal_selector_3_r0), .in_5(n5_signal_selector_2_r0), .in_6(n5_signal_selector_1_r0), .R0(R0),
    .R1(R1), .R2(R2), .R3(R3), .OVERFLOW(OVERFLOW));
  // Probe on {R3, R2, R1, R0}
  and and_2 (ZERO, ~R0, ~R1, ~R2, ~R3);  // AND_Gate
endmodule

module AND (
  input  A0,
  input  A1,
  input  A2,
  input  A3,
  input  B0,
  input  B1,
  input  B2,
  input  B3,
  output R0,
  output R1,
  output R2,
  output R3
);

  and and_1 (R0, A0, B0);
  and and_2 (R1, A1, B1);
  and and_3 (R2, A2, B2);
  and and_4 (R3, A3, B3);
endmodule

module OR (
  input  A0,
  input  A1,
  input  A2,
  input  A3,
  input  B0,
  input  B1,
  input  B2,
  input  B3,
  output R0,
  output R1,
  output R2,
  output R3
);

  or or_1 (R0, A0, B0);
  or or_2 (R1, A1, B1);
  or or_3 (R2, A2, B2);
  or or_4 (R3, A3, B3);
endmodule

module ADD (
  input  CONTROL,
  input  A0,
  input  A1,
  input  A2,
  input  A3,
  input  B0,
  input  B1,
  input  B2,
  input  B3,
  output R0,
  output R1,
  output R2,
  output R3,
  output OVERFLOW
);

  wire and_1_out, and_2_out, n1_bit_adder_1_carry_out, n1_bit_adder_2_carry_out, n1_bit_adder_3_carry_out;

  // Probe on {A3, A2, A1, A0}
  // Probe on {B3, B2, B1, B0}
  _1_bit_adder u_1_bit_adder_1 (.A(A0), .B(B0), .Carry_in(CONTROL), .R(R0), .Carry_out(n1_bit_adder_1_carry_out));
  _1_bit_adder u_1_bit_adder_2 (
    .A(A1), .B(B1), .Carry_in(n1_bit_adder_1_carry_out), .R(R1), .Carry_out(n1_bit_adder_2_carry_out));
  _1_bit_adder u_1_bit_adder_3 (
    .A(A2), .B(B2), .Carry_in(n1_bit_adder_2_carry_out), .R(R2), .Carry_out(n1_bit_adder_3_carry_out));
  _1_bit_adder u_1_bit_adder_4 (.A(A3), .B(B3), .Carry_in(n1_bit_adder_3_carry_out), .R(R3));  // open: Carry_out
  and and_1 (and_1_out, R3, ~B3, ~A3);  // AND_Gate
  and and_2 (and_2_out, ~R3, B3, A3);  // AND_Gate
  // Probe on {R3, R2, R1, R0}
  or or_1 (OVERFLOW, and_1_out, and_2_out);
endmodule

module SUB (
  input  A0,
  input  A1,
  input  A2,
  input  A3,
  input  B0,
  input  B1,
  input  B2,
  input  B3,
  output R0,
  output R1,
  output R2,
  output R3,
  output OVERFLOW
);

  wire not_1_out, not_2_out, not_3_out, not_4_out;

  // Probe on {A3, A2, A1, A0}
  not not_1 (not_1_out, B0);
  not not_2 (not_2_out, B1);
  not not_3 (not_3_out, B2);
  not not_4 (not_4_out, B3);
  // Probe on {B3, B2, B1, B0}
  // Probe on {R3, R2, R1, R0}
  ADD add_1 (
    .CONTROL(1'b1), .A0(A0), .A1(A1), .A2(A2), .A3(A3), .B0(not_1_out), .B1(not_2_out), .B2(not_3_out),
    .B3(not_4_out), .R0(R0), .R1(R1), .R2(R2), .R3(R3), .OVERFLOW(OVERFLOW));
endmodule

module SLT (
  input  A0,
  input  A1,
  input  A2,
  input  A3,
  input  B0,
  input  B1,
  input  B2,
  input  B3,
  output R0,
  output R1,
  output R2,
  output R3,
  output OVERFLOW
);

  wire sub_1_overflow, sub_1_r3;

  // Probe on {A3, A2, A1, A0}
  // Probe on {B3, B2, B1, B0}
  SUB sub_1 (
    .A0(A0), .A1(A1), .A2(A2), .A3(A3), .B0(B0), .B1(B1), .B2(B2), .B3(B3), .R3(sub_1_r3),
    .OVERFLOW(sub_1_overflow));  // open: R0, R1, R2
  or or_1 (R0, sub_1_r3, sub_1_overflow);

  assign OVERFLOW = 1'b0;
  assign R1 = 1'b0;
  assign R2 = 1'b0;
  assign R3 = 1'b0;
endmodule

module NOR (
  input  A0,
  input  A1,
  input  A2,
  input  A3,
  input  B0,
  input  B1,
  input  B2,
  input  B3,
  output R0,
  output R1,
  output R2,
  output R3
);

  nor nor_1 (R0, A0, B0);
  nor nor_2 (R1, A1, B1);
  nor nor_3 (R2, A2, B2);
  nor nor_4 (R3, A3, B3);
endmodule

// Control Signal Decoder
module _4_bit_control_signal_decoder (
  input  C0,
  input  C1,
  input  C2,
  input  C3,
  output [3:0] out_5,
  output AND,
  output OR,
  output ADD,
  output SUB,
  output SLT,
  output NOR
);

  and and_1 (AND, ~C0, ~C1, ~C2, ~C3);  // AND_Gate
  and and_2 (OR, C0, ~C1, ~C2, ~C3);  // AND_Gate
  and and_3 (ADD, ~C0, C1, ~C2, ~C3);  // AND_Gate
  and and_4 (SUB, ~C0, C1, C2, ~C3);  // AND_Gate
  and and_5 (SLT, C0, C1, C2, ~C3);  // AND_Gate
  and and_6 (NOR, ~C0, ~C1, C2, C3);  // AND_Gate

  assign out_5 = {C3, C2, C1, C0};
endmodule

module _1_bit_adder (
  input  A,
  input  B,
  input  Carry_in,
  output R,
  output Carry_out
);

  wire and_1_out, and_2_out, and_3_out, and_4_out, and_5_out, and_6_out, and_7_out;

  and and_1 (and_1_out, A, ~B, ~Carry_in);  // AND_Gate
  and and_2 (and_2_out, ~A, B, ~Carry_in);  // AND_Gate
  and and_3 (and_3_out, ~A, ~B, Carry_in);  // AND_Gate
  and and_4 (and_4_out, A, B, Carry_in);
  and and_5 (and_5_out, A, B);
  and and_6 (and_6_out, A, Carry_in);
  and and_7 (and_7_out, B, Carry_in);
  or or_1 (R, and_1_out, and_2_out, and_3_out, and_4_out);
  or or_2 (Carry_out, and_5_out, and_6_out, and_7_out);
endmodule

// Signal selector
module _5_signal_selector (
  input  _0,
  input  _1,
  input  _2,
  input  _3,
  input  OVERFLOW,
  input  S,
  output R0,
  output R1,
  output R2,
  output R3,
  output OVERFLOW_2
);

  and and_1 (R0, _0, S);
  and and_2 (R1, _1, S);
  and and_3 (R2, _2, S);
  and and_4 (R3, _3, S);
  and and_5 (OVERFLOW_2, OVERFLOW, S);
endmodule

// Signal merger
module _5_signl_merger (
  input  [4:0] in_1,
  input  [4:0] in_2,
  input  [4:0] in_3,
  input  [4:0] in_4,
  input  [4:0] in_5,
  input  [4:0] in_6,
  output R0,
  output R1,
  output R2,
  output R3,
  output OVERFLOW
);

  or or_1 (R0, in_1[0], in_2[0], in_3[0], in_4[0], in_5[0], in_6[0]);
  or or_2 (R1, in_1[1], in_2[1], in_3[1], in_4[1], in_5[1], in_6[1]);
  or or_3 (R2, in_1[2], in_2[2], in_3[2], in_4[2], in_5[2], in_6[2]);
  or or_4 (R3, in_1[3], in_2[3], in_3[3], in_4[3], in_5[3], in_6[3]);
  or or_5 (OVERFLOW, in_1[4], in_2[4], in_3[4], in_4[4], in_5[4], in_6[4]);
endmodule
