// Logisim project COMP273Assignment2.circ as structural Verilog: 4 circuits, main circuit main
module main (
  input  RESET__TURN_ON_TO_MULTIPLY,
  input  [7:0] A__MULTIPLICAND,
  input  [7:0] B__MULTIPLIER,
  input  RESET__TURN_ON_TO_DIVIDE,
  input  [7:0] DIVISOR,
  input  [7:0] DIVIDEND,
  output DONE,
  output DONE_2
);

  wire _32_HZ_out, and_1_out, CLOCK_2_out, CLOCK_out, counter_1_carry, counter_2_carry, not_1_out, not_2_out,
       not_3_out, not_4_out, not_5_out, not_6_out, not_7_out, not_8_out, not_9_out, not_10_out, not_11_out,
       not_12_out, not_13_out, not_14_out, not_15_out, not_16_out, not_17_out, not_18_out, not_19_out,
       not_20_out, not_21_out, not_22_out, not_23_out, not_24_out, not_25_out, not_26_out, not_27_out,
       not_28_out, not_29_out, not_30_out, not_31_out, not_32_out, not_33_out, not_34_out, not_35_out,
       not_36_out, not_37_out, not_38_out, not_39_out, not_40_out, not_41_out, not_42_out, not_43_out,
       not_44_out, not_45_out, or_1_out, or_2_out, or_3_out, or_4_out, or_5_out, or_6_out, or_7_out,
       or_8_out, or_9_out, PRESS_TO_RESET_out, shift_register_1_out, shift_register_1_q0,
       shift_register_1_q1, shift_register_1_q2, shift_register_1_q3, shift_register_1_q4,
       shift_register_1_q5, shift_register_1_q6, shift_register_1_q7, shift_register_2_out,
       shift_register_3_out, shift_register_3_q0, shift_register_3_q1, shift_register_3_q2,
       shift_register_3_q3, shift_register_3_q4, shift_register_3_q5, shift_register_3_q6,
       shift_register_3_q7, subtractor_1_bout;
  wire [7:0] QUOTIENT_q0;
  wire [15:0] adder_1_out, bitselector_1_out, DIVISOR_q15, multiplexer_1_out,
       READ_BITS_FROM_RIGHT_TO_LEFT_q0, register_1_q, REMAINDER_q, subtractor_1_out;

  Button PRESS_TO_RESET (.out(PRESS_TO_RESET_out));
  Clock _32_HZ (.out(_32_HZ_out));
  Shift_Register shift_register_1 (
    .in(shift_register_3_out), .clk(_32_HZ_out), .out(shift_register_1_out), .load(PRESS_TO_RESET_out),
    .d0(PRESS_TO_RESET_out), .q0(shift_register_1_q0), .d1(PRESS_TO_RESET_out), .q1(shift_register_1_q1),
    .d2(PRESS_TO_RESET_out), .q2(shift_register_1_q2), .d3(not_2_out), .q3(shift_register_1_q3),
    .d4(not_5_out), .q4(shift_register_1_q4), .d5(not_4_out), .q5(shift_register_1_q5), .d6(not_3_out),
    .q6(shift_register_1_q6), .d7(not_1_out), .q7(shift_register_1_q7));  // open: shift, clr
  Clock CLOCK (.out(CLOCK_out));
  not not_1 (not_1_out, PRESS_TO_RESET_out);
  not not_2 (not_2_out, PRESS_TO_RESET_out);
  not not_3 (not_3_out, PRESS_TO_RESET_out);
  not not_4 (not_4_out, PRESS_TO_RESET_out);
  not not_5 (not_5_out, PRESS_TO_RESET_out);
  or or_1 (or_1_out, shift_register_1_q0, shift_register_3_q7);
  or or_2 (or_2_out, shift_register_1_q2, shift_register_3_q5);
  or or_3 (or_3_out, shift_register_1_q1, shift_register_3_q6);
  LED led_1 (.in(or_1_out));
  LED led_2 (.in(or_2_out));
  LED led_3 (.in(or_3_out));
  not not_6 (not_6_out, RESET__TURN_ON_TO_MULTIPLY);
  // Probe on A__MULTIPLICAND
  // Probe on B__MULTIPLIER
  Clock CLOCK_2 (.out(CLOCK_2_out));
  not not_7 (not_7_out, RESET__TURN_ON_TO_DIVIDE);
  // Probe on DIVISOR
  // Probe on DIVIDEND
  or or_4 (or_4_out, shift_register_1_q4, shift_register_3_q3);
  or or_5 (or_5_out, shift_register_1_q3, shift_register_3_q4);
  or or_6 (or_6_out, shift_register_1_q5, shift_register_3_q2);
  LED led_4 (.in(or_5_out));
  LED led_5 (.in(or_6_out));
  LED led_6 (.in(or_4_out));
  Shift_Register #(.length(16)) READ_BITS_FROM_RIGHT_TO_LEFT (
    .in(not_6_out), .clk(CLOCK_out), .load(not_6_out), .d0(A__MULTIPLICAND[0]),
    .q0(READ_BITS_FROM_RIGHT_TO_LEFT_q0[0]), .d1(A__MULTIPLICAND[1]),
    .q1(READ_BITS_FROM_RIGHT_TO_LEFT_q0[1]), .d2(A__MULTIPLICAND[2]),
    .q2(READ_BITS_FROM_RIGHT_TO_LEFT_q0[2]), .d3(A__MULTIPLICAND[3]),
    .q3(READ_BITS_FROM_RIGHT_TO_LEFT_q0[3]), .d4(A__MULTIPLICAND[4]),
    .q4(READ_BITS_FROM_RIGHT_TO_LEFT_q0[4]), .d5(A__MULTIPLICAND[5]),
    .q5(READ_BITS_FROM_RIGHT_TO_LEFT_q0[5]), .d6(A__MULTIPLICAND[6]),
    .q6(READ_BITS_FROM_RIGHT_TO_LEFT_q0[6]), .d7(A__MULTIPLICAND[7]),
    .q7(READ_BITS_FROM_RIGHT_TO_LEFT_q0[7]), .d8(not_11_out), .q8(READ_BITS_FROM_RIGHT_TO_LEFT_q0[8]),
    .d9(not_13_out), .q9(READ_BITS_FROM_RIGHT_TO_LEFT_q0[9]), .d10(not_12_out),
    .q10(READ_BITS_FROM_RIGHT_TO_LEFT_q0[10]), .d11(not_33_out), .q11(READ_BITS_FROM_RIGHT_TO_LEFT_q0[11]),
    .d12(not_35_out), .q12(READ_BITS_FROM_RIGHT_TO_LEFT_q0[12]), .d13(not_36_out),
    .q13(READ_BITS_FROM_RIGHT_TO_LEFT_q0[13]), .d14(not_34_out), .q14(READ_BITS_FROM_RIGHT_TO_LEFT_q0[14]),
    .d15(not_37_out), .q15(READ_BITS_FROM_RIGHT_TO_LEFT_q0[15]));  // open: shift, out, clr
  Shift_Register shift_register_2 (
    .in(not_6_out), .clk(CLOCK_out), .out(shift_register_2_out), .load(not_6_out), .d0(B__MULTIPLIER[7]),
    .d1(B__MULTIPLIER[6]), .d2(B__MULTIPLIER[5]), .d3(B__MULTIPLIER[4]), .d4(B__MULTIPLIER[3]),
    .d5(B__MULTIPLIER[2]), .d6(B__MULTIPLIER[1]), .d7(B__MULTIPLIER[0]));  // open: shift, clr, q0, q1, q2, q3, q4, q5, q6, q7
  Shift_Register #(.length(16)) u_DIVISOR (
    .in(not_7_out), .clk(CLOCK_2_out), .load(not_7_out), .d0(DIVIDEND[7]), .q0(DIVISOR_q15[15]),
    .d1(DIVIDEND[6]), .q1(DIVISOR_q15[14]), .d2(DIVIDEND[5]), .q2(DIVISOR_q15[13]), .d3(DIVIDEND[4]),
    .q3(DIVISOR_q15[12]), .d4(DIVIDEND[3]), .q4(DIVISOR_q15[11]), .d5(DIVIDEND[2]), .q5(DIVISOR_q15[10]),
    .d6(DIVIDEND[1]), .q6(DIVISOR_q15[9]), .d7(DIVIDEND[0]), .q7(DIVISOR_q15[8]), .d8(not_14_out),
    .q8(DIVISOR_q15[7]), .d9(not_15_out), .q9(DIVISOR_q15[6]), .d10(not_16_out), .q10(DIVISOR_q15[5]),
    .d11(not_40_out), .q11(DIVISOR_q15[4]), .d12(not_42_out), .q12(DIVISOR_q15[3]), .d13(not_38_out),
    .q13(DIVISOR_q15[2]), .d14(not_41_out), .q14(DIVISOR_q15[1]), .d15(not_39_out), .q15(DIVISOR_q15[0]));  // open: shift, out, clr
  not not_8 (not_8_out, not_7_out);
  not not_9 (not_9_out, PRESS_TO_RESET_out);
  not not_10 (not_10_out, PRESS_TO_RESET_out);
  Shift_Register shift_register_3 (
    .in(shift_register_1_out), .clk(_32_HZ_out), .out(shift_register_3_out), .load(PRESS_TO_RESET_out),
    .d0(not_10_out), .q0(shift_register_3_q0), .d1(not_9_out), .q1(shift_register_3_q1), .d2(not_30_out),
    .q2(shift_register_3_q2), .d3(not_29_out), .q3(shift_register_3_q3), .d4(not_27_out),
    .q4(shift_register_3_q4), .d5(not_28_out), .q5(shift_register_3_q5), .d6(not_32_out),
    .q6(shift_register_3_q6), .d7(not_31_out), .q7(shift_register_3_q7));  // open: shift, clr
  or or_7 (or_7_out, shift_register_1_q7, shift_register_3_q0);
  or or_8 (or_8_out, shift_register_1_q6, shift_register_3_q1);
  LED led_7 (.in(or_8_out));
  LED led_8 (.in(or_7_out));
  not not_11 (not_11_out, not_6_out);
  not not_12 (not_12_out, not_6_out);
  not not_13 (not_13_out, not_6_out);
  not not_14 (not_14_out, not_7_out);
  not not_15 (not_15_out, not_7_out);
  not not_16 (not_16_out, not_7_out);
  not not_17 (not_17_out, not_7_out);
  not not_18 (not_18_out, not_7_out);
  not not_19 (not_19_out, not_7_out);
  not not_20 (not_20_out, not_7_out);
  not not_21 (not_21_out, not_7_out);
  not not_22 (not_22_out, not_7_out);
  not not_23 (not_23_out, DONE_2);
  not not_24 (not_24_out, subtractor_1_bout);
  Shift_Register QUOTIENT (
    .shift(not_23_out), .in(not_24_out), .clk(CLOCK_2_out), .load(not_7_out), .d0(not_22_out),
    .q0(QUOTIENT_q0[0]), .d1(not_20_out), .q1(QUOTIENT_q0[1]), .d2(not_21_out), .q2(QUOTIENT_q0[2]),
    .d3(not_18_out), .q3(QUOTIENT_q0[3]), .d4(not_19_out), .q4(QUOTIENT_q0[4]), .d5(not_17_out),
    .q5(QUOTIENT_q0[5]), .d6(not_44_out), .q6(QUOTIENT_q0[6]), .d7(not_43_out), .q7(QUOTIENT_q0[7]));  // open: out, clr
  not not_25 (not_25_out, subtractor_1_bout);
  or or_9 (or_9_out, not_25_out, not_7_out);
  not not_26 (not_26_out, DONE_2);
  D_Flip_Flop d_ff_1 (
    .clk(CLOCK_2_out), .Q(DONE_2), .preset(counter_1_carry), .en(not_7_out), .reset(not_7_out));  // open: D, Qn
  Counter #(.width(4), .max('hf)) counter_1 (
    .load(not_7_out), .D(4'b0110), .count(not_8_out), .carry(counter_1_carry), .clk(CLOCK_2_out));  // open: Q, clr
  not not_27 (not_27_out, PRESS_TO_RESET_out);
  not not_28 (not_28_out, PRESS_TO_RESET_out);
  not not_29 (not_29_out, PRESS_TO_RESET_out);
  not not_30 (not_30_out, PRESS_TO_RESET_out);
  not not_31 (not_31_out, PRESS_TO_RESET_out);
  not not_32 (not_32_out, PRESS_TO_RESET_out);
  not not_33 (not_33_out, not_6_out);
  not not_34 (not_34_out, not_6_out);
  not not_35 (not_35_out, not_6_out);
  not not_36 (not_36_out, not_6_out);
  not not_37 (not_37_out, not_6_out);
  Counter #(.width(3), .max('h7)) counter_2 (
    .count(1'b1), .carry(counter_2_carry), .clk(CLOCK_out), .clr(not_6_out));  // open: load, D, Q
  not not_38 (not_38_out, not_7_out);
  not not_39 (not_39_out, not_7_out);
  not not_40 (not_40_out, not_7_out);
  not not_41 (not_41_out, not_7_out);
  not not_42 (not_42_out, not_7_out);
  not not_43 (not_43_out, not_7_out);
  not not_44 (not_44_out, not_7_out);
  and and_1 (and_1_out, or_9_out, not_26_out);
  BitSelector #(.width(16), .group(16)) bitselector_1 (
    .in(READ_BITS_FROM_RIGHT_TO_LEFT_q0), .out(bitselector_1_out), .sel(not_45_out));
  not not_45 (not_45_out, shift_register_2_out);
  Register #(.width(16)) register_1 (.D(adder_1_out), .Q(register_1_q), .clk(CLOCK_out), .clr(not_6_out));  // open: en
  D_Flip_Flop d_ff_2 (
    .clk(CLOCK_out), .Q(DONE), .preset(counter_2_carry), .en(not_6_out), .reset(not_6_out));  // open: D, Qn
  Subtractor #(.width(16)) subtractor_1 (
    .a(REMAINDER_q), .b(DIVISOR_q15), .out(subtractor_1_out), .bin(1'b0), .bout(subtractor_1_bout));
  Register #(.width(16)) REMAINDER (
    .D(multiplexer_1_out), .en(and_1_out), .Q(REMAINDER_q), .clk(CLOCK_2_out));  // open: clr
  Multiplexer #(.width(16)) multiplexer_1 (
    .in0(subtractor_1_out), .in1({{8{1'b0}}, DIVISOR}), .out(multiplexer_1_out), .sel(not_7_out));  // open: en
  Adder #(.width(16)) adder_1 (.a(bitselector_1_out), .b(register_1_q), .out(adder_1_out));  // open: cin, cout
  // Probe on adder_1_out
  // Probe on QUOTIENT_q0
  // Probe on REMAINDER_q

  // Notes on the sheet:
  //   QUESTION 1
  //   QUESTION 2
  //   QUESTION 3
  //   DAVID YANG ZHOU 260517397
endmodule

module QUESTION_1 (
);

  wire _32_HZ_out, not_1_out, not_2_out, not_3_out, not_4_out, not_5_out, not_6_out, not_7_out, not_8_out,
       not_9_out, not_10_out, not_11_out, not_12_out, not_13_out, or_1_out, or_2_out, or_3_out, or_4_out,
       or_5_out, or_6_out, or_7_out, or_8_out, PRESS_TO_RESET_out, shift_register_1_out, shift_register_1_q0,
       shift_register_1_q1, shift_register_1_q2, shift_register_1_q3, shift_register_1_q4,
       shift_register_1_q5, shift_register_1_q6, shift_register_1_q7, shift_register_2_out,
       shift_register_2_q0, shift_register_2_q1, shift_register_2_q2, shift_register_2_q3,
       shift_register_2_q4, shift_register_2_q5, shift_register_2_q6, shift_register_2_q7;

  Button PRESS_TO_RESET (.out(PRESS_TO_RESET_out));
  Clock _32_HZ (.out(_32_HZ_out));
  Shift_Register shift_register_1 (
    .in(shift_register_2_out), .clk(_32_HZ_out), .out(shift_register_1_out), .load(PRESS_TO_RESET_out),
    .d0(PRESS_TO_RESET_out), .q0(shift_register_1_q0), .d1(PRESS_TO_RESET_out), .q1(shift_register_1_q1),
    .d2(PRESS_TO_RESET_out), .q2(shift_register_1_q2), .d3(not_1_out), .q3(shift_register_1_q3),
    .d4(not_3_out), .q4(shift_register_1_q4), .d5(not_4_out), .q5(shift_register_1_q5), .d6(not_2_out),
    .q6(shift_register_1_q6), .d7(not_5_out), .q7(shift_register_1_q7));  // open: shift, clr
  not not_1 (not_1_out, PRESS_TO_RESET_out);
  not not_2 (not_2_out, PRESS_TO_RESET_out);
  not not_3 (not_3_out, PRESS_TO_RESET_out);
  not not_4 (not_4_out, PRESS_TO_RESET_out);
  or or_1 (or_1_out, shift_register_1_q1, shift_register_2_q6);
  or or_2 (or_2_out, shift_register_1_q0, shift_register_2_q7);
  LED led_1 (.in(or_1_out));
  LED led_2 (.in(or_2_out));
  not not_5 (not_5_out, PRESS_TO_RESET_out);
  or or_3 (or_3_out, shift_register_1_q4, shift_register_2_q3);
  or or_4 (or_4_out, shift_register_1_q3, shift_register_2_q4);
  or or_5 (or_5_out, shift_register_1_q2, shift_register_2_q5);
  LED led_3 (.in(or_5_out));
  LED led_4 (.in(or_4_out));
  LED led_5 (.in(or_3_out));
  Shift_Register shift_register_2 (
    .in(shift_register_1_out), .clk(_32_HZ_out), .out(shift_register_2_out), .load(PRESS_TO_RESET_out),
    .d0(not_8_out), .q0(shift_register_2_q0), .d1(not_9_out), .q1(shift_register_2_q1), .d2(not_10_out),
    .q2(shift_register_2_q2), .d3(not_12_out), .q3(shift_register_2_q3), .d4(not_7_out),
    .q4(shift_register_2_q4), .d5(not_6_out), .q5(shift_register_2_q5), .d6(not_11_out),
    .q6(shift_register_2_q6), .d7(not_13_out), .q7(shift_register_2_q7));  // open: shift, clr
  or or_6 (or_6_out, shift_register_1_q5, shift_register_2_q2);
  or or_7 (or_7_out, shift_register_1_q6, shift_register_2_q1);
  LED led_6 (.in(or_7_out));
  LED led_7 (.in(or_6_out));
  not not_6 (not_6_out, PRESS_TO_RESET_out);
  not not_7 (not_7_out, PRESS_TO_RESET_out);
  not not_8 (not_8_out, PRESS_TO_RESET_out);
  not not_9 (not_9_out, PRESS_TO_RESET_out);
  not not_10 (not_10_out, PRESS_TO_RESET_out);
  not not_11 (not_11_out, PRESS_TO_RESET_out);
  not not_12 (not_12_out, PRESS_TO_RESET_out);
  or or_8 (or_8_out, shift_register_1_q7, shift_register_2_q0);
  LED led_8 (.in(or_8_out));
  not not_13 (not_13_out, PRESS_TO_RESET_out);
endmodule

module QUESTION_2 (
  input  RESET__TURN_ON_TO_MULTIPLY,
  input  [7:0] A__MULTIPLICAND,
  input  [7:0] B__MULTIPLIER,
  output DONE
);

  wire CLOCK_out, counter_1_carry, not_1_out, not_2_out, not_3_out, not_4_out, not_5_out, not_6_out,
       not_7_out, not_8_out, not_9_out, not_10_out, shift_register_1_out;
  wire [15:0] adder_1_out, bitselector_1_out, READ_BITS_FROM_RIGHT_TO_LEFT_q0, register_1_q;

  Clock CLOCK (.out(CLOCK_out));
  // Probe on A__MULTIPLICAND
  // Probe on B__MULTIPLIER
  not not_1 (not_1_out, RESET__TURN_ON_TO_MULTIPLY);
  Shift_Register #(.length(16)) READ_BITS_FROM_RIGHT_TO_LEFT (
    .in(not_1_out), .clk(CLOCK_out), .load(not_1_out), .d0(A__MULTIPLICAND[0]),
    .q0(READ_BITS_FROM_RIGHT_TO_LEFT_q0[0]), .d1(A__MULTIPLICAND[1]),
    .q1(READ_BITS_FROM_RIGHT_TO_LEFT_q0[1]), .d2(A__MULTIPLICAND[2]),
    .q2(READ_BITS_FROM_RIGHT_TO_LEFT_q0[2]), .d3(A__MULTIPLICAND[3]),
    .q3(READ_BITS_FROM_RIGHT_TO_LEFT_q0[3]), .d4(A__MULTIPLICAND[4]),
    .q4(READ_BITS_FROM_RIGHT_TO_LEFT_q0[4]), .d5(A__MULTIPLICAND[5]),
    .q5(READ_BITS_FROM_RIGHT_TO_LEFT_q0[5]), .d6(A__MULTIPLICAND[6]),
    .q6(READ_BITS_FROM_RIGHT_TO_LEFT_q0[6]), .d7(A__MULTIPLICAND[7]),
    .q7(READ_BITS_FROM_RIGHT_TO_LEFT_q0[7]), .d8(not_5_out), .q8(READ_BITS_FROM_RIGHT_TO_LEFT_q0[8]),
    .d9(not_3_out), .q9(READ_BITS_FROM_RIGHT_TO_LEFT_q0[9]), .d10(not_4_out),
    .q10(READ_BITS_FROM_RIGHT_TO_LEFT_q0[10]), .d11(not_2_out), .q11(READ_BITS_FROM_RIGHT_TO_LEFT_q0[11]),
    .d12(not_8_out), .q12(READ_BITS_FROM_RIGHT_TO_LEFT_q0[12]), .d13(not_6_out),
    .q13(READ_BITS_FROM_RIGHT_TO_LEFT_q0[13]), .d14(not_7_out), .q14(READ_BITS_FROM_RIGHT_TO_LEFT_q0[14]),
    .d15(not_9_out), .q15(READ_BITS_FROM_RIGHT_TO_LEFT_q0[15]));  // open: shift, out, clr
  Shift_Register shift_register_1 (
    .in(not_1_out), .clk(CLOCK_out), .out(shift_register_1_out), .load(not_1_out), .d0(B__MULTIPLIER[7]),
    .d1(B__MULTIPLIER[6]), .d2(B__MULTIPLIER[5]), .d3(B__MULTIPLIER[4]), .d4(B__MULTIPLIER[3]),
    .d5(B__MULTIPLIER[2]), .d6(B__MULTIPLIER[1]), .d7(B__MULTIPLIER[0]));  // open: shift, clr, q0, q1, q2, q3, q4, q5, q6, q7
  not not_2 (not_2_out, not_1_out);
  not not_3 (not_3_out, not_1_out);
  not not_4 (not_4_out, not_1_out);
  not not_5 (not_5_out, not_1_out);
  not not_6 (not_6_out, not_1_out);
  not not_7 (not_7_out, not_1_out);
  not not_8 (not_8_out, not_1_out);
  not not_9 (not_9_out, not_1_out);
  Counter #(.width(3), .max('h7)) counter_1 (
    .count(1'b1), .carry(counter_1_carry), .clk(CLOCK_out), .clr(not_1_out));  // open: load, D, Q
  BitSelector #(.width(16), .group(16)) bitselector_1 (
    .in(READ_BITS_FROM_RIGHT_TO_LEFT_q0), .out(bitselector_1_out), .sel(not_10_out));
  not not_10 (not_10_out, shift_register_1_out);
  Adder #(.width(16)) adder_1 (.a(bitselector_1_out), .b(register_1_q), .out(adder_1_out));  // open: cin, cout
  Register #(.width(16)) register_1 (.D(adder_1_out), .Q(register_1_q), .clk(CLOCK_out), .clr(not_1_out));  // open: en
  D_Flip_Flop d_ff_1 (
    .clk(CLOCK_out), .Q(DONE), .preset(counter_1_carry), .en(not_1_out), .reset(not_1_out));  // open: D, Qn
  // Probe on adder_1_out
endmodule

module QUESTION_3 (
  input  RESET__TURN_ON_TO_DIVIDE,
  input  [7:0] DIVISOR,
  input  [7:0] DIVIDEND,
  output DONE
);

  wire and_1_out, CLOCK_out, counter_1_carry, not_1_out, not_2_out, not_3_out, not_4_out, not_5_out,
       not_6_out, not_7_out, not_8_out, not_9_out, not_10_out, not_11_out, not_12_out, not_13_out,
       not_14_out, not_15_out, not_16_out, not_17_out, not_18_out, not_19_out, not_20_out, not_21_out,
       not_22_out, or_1_out, subtractor_1_bout;
  wire [7:0] QUOTIENT_q0;
  wire [15:0] DIVISOR_q15, multiplexer_1_out, REMAINDER_2_q, subtractor_1_out;

  Clock CLOCK (.out(CLOCK_out));
  not not_1 (not_1_out, RESET__TURN_ON_TO_DIVIDE);
  // Probe on DIVISOR
  // Probe on DIVIDEND
  Shift_Register #(.length(16)) u_DIVISOR (
    .in(not_1_out), .clk(CLOCK_out), .load(not_1_out), .d0(DIVIDEND[7]), .q0(DIVISOR_q15[15]),
    .d1(DIVIDEND[6]), .q1(DIVISOR_q15[14]), .d2(DIVIDEND[5]), .q2(DIVISOR_q15[13]), .d3(DIVIDEND[4]),
    .q3(DIVISOR_q15[12]), .d4(DIVIDEND[3]), .q4(DIVISOR_q15[11]), .d5(DIVIDEND[2]), .q5(DIVISOR_q15[10]),
    .d6(DIVIDEND[1]), .q6(DIVISOR_q15[9]), .d7(DIVIDEND[0]), .q7(DIVISOR_q15[8]), .d8(not_11_out),
    .q8(DIVISOR_q15[7]), .d9(not_10_out), .q9(DIVISOR_q15[6]), .d10(not_8_out), .q10(DIVISOR_q15[5]),
    .d11(not_9_out), .q11(DIVISOR_q15[4]), .d12(not_7_out), .q12(DIVISOR_q15[3]), .d13(not_12_out),
    .q13(DIVISOR_q15[2]), .d14(not_21_out), .q14(DIVISOR_q15[1]), .d15(not_22_out), .q15(DIVISOR_q15[0]));  // open: shift, out, clr
  not not_2 (not_2_out, not_1_out);
  not not_3 (not_3_out, DONE);
  Shift_Register QUOTIENT (
    .shift(not_3_out), .in(not_4_out), .clk(CLOCK_out), .load(not_1_out), .d0(not_2_out),
    .q0(QUOTIENT_q0[0]), .d1(not_16_out), .q1(QUOTIENT_q0[1]), .d2(not_13_out), .q2(QUOTIENT_q0[2]),
    .d3(not_14_out), .q3(QUOTIENT_q0[3]), .d4(not_19_out), .q4(QUOTIENT_q0[4]), .d5(not_17_out),
    .q5(QUOTIENT_q0[5]), .d6(not_18_out), .q6(QUOTIENT_q0[6]), .d7(not_15_out), .q7(QUOTIENT_q0[7]));  // open: out, clr
  not not_4 (not_4_out, subtractor_1_bout);
  not not_5 (not_5_out, subtractor_1_bout);
  Counter #(.width(4), .max('hf)) counter_1 (
    .load(not_1_out), .D(4'b0110), .count(not_6_out), .carry(counter_1_carry), .clk(CLOCK_out));  // open: Q, clr
  not not_6 (not_6_out, not_1_out);
  not not_7 (not_7_out, not_1_out);
  not not_8 (not_8_out, not_1_out);
  not not_9 (not_9_out, not_1_out);
  not not_10 (not_10_out, not_1_out);
  not not_11 (not_11_out, not_1_out);
  not not_12 (not_12_out, not_1_out);
  not not_13 (not_13_out, not_1_out);
  not not_14 (not_14_out, not_1_out);
  not not_15 (not_15_out, not_1_out);
  not not_16 (not_16_out, not_1_out);
  not not_17 (not_17_out, not_1_out);
  not not_18 (not_18_out, not_1_out);
  not not_19 (not_19_out, not_1_out);
  or or_1 (or_1_out, not_5_out, not_1_out);
  and and_1 (and_1_out, or_1_out, not_20_out);
  not not_20 (not_20_out, DONE);
  D_Flip_Flop d_ff_1 (
    .clk(CLOCK_out), .Q(DONE), .preset(counter_1_carry), .en(not_1_out), .reset(not_1_out));  // open: D, Qn
  not not_21 (not_21_out, not_1_out);
  not not_22 (not_22_out, not_1_out);
  Multiplexer #(.width(16)) multiplexer_1 (
    .in0(subtractor_1_out), .in1({{8{1'b0}}, DIVISOR}), .out(multiplexer_1_out), .sel(not_1_out));  // open: en
  Subtractor #(.width(16)) subtractor_1 (
    .a(REMAINDER_2_q), .b(DIVISOR_q15), .out(subtractor_1_out), .bin(1'b0), .bout(subtractor_1_bout));
  // Probe on REMAINDER_2_q
  Register #(.width(16)) REMAINDER_2 (
    .D(multiplexer_1_out), .en(and_1_out), .Q(REMAINDER_2_q), .clk(CLOCK_out));  // open: clr
  // Probe on QUOTIENT_q0
endmodule
